# Fritzing sketch skematik (saved by Fritzing 0.9.3b)

parts:
  Part1 = Arduino Uno (Rev3)
  M1 = DC Motor
  M2 = DC Motor
  L298N1 = L298N DC motor driver
  VCC1 = Battery
  JACK1 = 2.1mm Barrel Jack with Terminal Block
  e-radionica_com1 = LM393 LDR breakout [part_number=100027]
  e-radionica_com2 = LM393 LDR breakout [part_number=100027]

nets:
  N1: Part1.D8, e-radionica_com2.DO
  N2: Part1.D9_PWM, e-radionica_com1.DO
  N3: Part1.D4, L298N1.IN1
  N4: Part1.D5_PWM, L298N1.IN2
  N5: Part1.D6_PWM, L298N1.IN3
  N6: Part1.D7, L298N1.IN4
  VCC: Part1.5V, e-radionica_com1.VCC, e-radionica_com2.VCC
  GND: Part1.GND, e-radionica_com1.GND, e-radionica_com2.GND
  N7: M1.pin_1, L298N1.OUT4
  N8: M1.pin_2, L298N1.OUT3
  N9: M2.pin_1, L298N1.OUT2
  N10: M2.pin_2, L298N1.OUT1
  N11: L298N1.12V, VCC1.+, JACK1.POS
  N12: L298N1.GND, VCC1.-, JACK1.NEG
  N13: L298N1.5V#9, L298N1.ENA
  N14: L298N1.5V#10, L298N1.ENB

custom parts:
  L298N DC motor driver: 2x DC motor driver with 78M05 positive voltage regulator (7..35 V) L298N: max 46 V, 2 A Set 5 V Enable jumper to enable 5 V regultor (needed for the L298N) and +5 V output at screw terminal or supply external +5 V at screw terminal Set ENA and/or ENB to +5 V to enable motor permanently or supply ENA and/or ENB with PWM signal IN1 and IN2 set rotation directory for motor A (OUT1/OUT2) IN2 and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
  Battery: Your standard 3x 18650 battery pack (11.1 Volts)
